// Digital circuit Lab00b.dig as structural Verilog
module Lab00b (
);

  wire switch1_b, switch2_b;

  Switch #(.Closed("true"), .switchActsAsInput("true")) switch1 (.A(1'b1), .B(switch1_b));
  Switch #(.Closed("true"), .switchActsAsInput("true")) switch2 (.A(switch1_b), .B(switch2_b));
  // PolarityAwareLED led1: pin names not known; wires that end beside it: switch2_b, 1'b0
endmodule
